# Fritzing sketch color-mixing-lamp (saved by Fritzing 0.9.3b)
breadboards: 1

parts:
  Arduino_UNO = Arduino Uno (Rev3)
  RGB_LED = RGB LED (com. anode, rbg) [package="5 mm [THT]"]
  R1 = Resistor [tolerance=±5% resistance=220 package=THT]
  R2 = Resistor [tolerance=±5% resistance=220 package=THT]
  R3 = Resistor [tolerance=±5% resistance=220 package=THT]
  Photocell_1 = PHOTOCELL [package=photocell-kit]
  Photocell_2 = PHOTOCELL [package=photocell-kit]
  Photocell_3 = PHOTOCELL [package=photocell-kit]
  R4 = Resistor [tolerance=±5% resistance=10k package=THT]
  R5 = Resistor [tolerance=±5% resistance=10k package=THT]
  R6 = Resistor [tolerance=±5% resistance=10k package=THT]

nets:
  N1: Arduino_UNO.A0, Photocell_1.P$1, R4.Pin_1
  N2: Arduino_UNO.A1, Photocell_2.P$1, R5.Pin_1
  N3: Arduino_UNO.A2, Photocell_3.P$1, R6.Pin_1
  N4: Arduino_UNO.D9_PWM, R3.Pin_0
  N5: Arduino_UNO.D10_PWM/SS, R1.Pin_0
  N6: Arduino_UNO.D11_PWM/MOSI, R2.Pin_0
  N7: Arduino_UNO.GND, R4.Pin_0, R5.Pin_0, R6.Pin_0
  N8: Arduino_UNO.5V, Photocell_1.P$2, Photocell_2.P$2, Photocell_3.P$2
  N9: RGB_LED.red_cathode, R1.Pin_1
  N10: RGB_LED.blue_cathode, R2.Pin_1
  N11: RGB_LED.green_cathode, R3.Pin_1

// code stored in the sketch: color-mixing-lamp.ino
//****************************************************************************
//
// Project Name: Arduino Projects Book - Project 04: Color Mixing Lamp
//
// File Name: color_mixing_lamp.ino
//
// Description: Indicate different colors on the RGB LED
// according to the amount of light each photocell receives
//
// Compatibility: Arduino UNO
//
// Phi Luu
// Portland, Oregon, United States
// Created October 25, 2015
// Updated August 13, 2016
//
//****************************************************************************

//**********Required Hardware I/O Connections**********
const byte redLEDPin = 11;       // connect red pin of the RGB LED to ~11
const byte blueLEDPin = 10;      // connect green pin of the RGB LED to ~10
const byte greenLEDPin = 9;      // connect blue pin of the RGB LED to ~9
const byte redSensorPin = A0;    // connect red sensor to A0
const byte greenSensorPin = A1;  // connect green sensor to A1
const byte blueSensorPin = A2;   // connect blue sensor to A2

// baud rate for serial monitor
const unsigned int BAUD_RATE = 9600;

// initial values
unsigned int redLEDValue = 0;           // init redLEDValue = 0
unsigned int blueLEDValue = 0;          // init blueLEDValue = 0
unsigned int greenLEDValue = 0;         // init greenLEDValue = 0
unsigned int redSensorValue = 0;        // init redSensorValue = 0
unsigned int blueSensorValue = 0;       // init blueSensorValue = 0
unsigned int greenSensorValue = 0;      // init greenSensorValue = 0

//**********setup**********
// Put setup code here, to run once
// Inputs: None
// Outputs: None
void setup() {
    Serial.begin(BAUD_RATE);            // start serial monitor
    pinMode(redLEDPin, OUTPUT);         // set redLEDPin as OUTPUT
    pinMode(blueLEDPin, OUTPUT);        // set blueLEDPin as OUTPUT
    pinMode(greenLEDPin, OUTPUT);       // set greenLEDPin as OUTPUT
}

//**********loop**********
// Put main code here, to run repeatedly
// Inputs: None
// Outputs: None
void loop() {
    // read the values from the sensors
    // leave 5 miliseconds for Analog - Digital Conversion
    redSensorValue = analogRead(redSensorPin);      // read redSensorPin
    delay(5);               // delay helps Arduino stable after reading
    blueSensorValue = analogRead(blueSensorPin);    // read blueSensorPin
    delay(5);               // delay helps Arduino stable after reading
    greenSensorValue = analogRead(greenSensorPin);  // read greenSensorPin

    // print those values onto the serial monitor
    Serial.println("Raw Sensor Values:");
    Serial.print("\t Red: ");
    Serial.print(redSensorValue);           // print redSensorValue
    Serial.print("\t Blue: ");
    Serial.print(blueSensorValue);          // print blueSensorValue
    Serial.print("\t Green: ");
    Serial.println(greenSensorValue);       // print greenSensorValue

    // convert from 0-1023 to 0-255 by divided by 4
    redLEDValue = redSensorValue/4;         // define Red LED
    blueLEDValue = blueSensorValue/4;       // define Blue LED
    greenLEDValue = greenSensorValue/4;     // define Green LED

    // print mapped values to serial monitor
    Serial.println("Mapped Sensor Values:");
    Serial.print("\t Red: ");
    Serial.print(redLEDValue);              // print redLEDValue
    Serial.print("\t Blue: ");
    Serial.print(blueLEDValue);             // print blueLEDValue
    Serial.print("\t Green: ");
    Serial.println(greenLEDValue);          // print greenLEDValue

    // use analogWrite() to set output for RGB LED
    analogWrite(redLEDPin, redLEDValue);          // indicate red LED
    analogWrite(blueLEDPin, blueLEDValue);        // indicate blue LED
    analogWrite(greenLEDPin, greenLEDValue);      // indicate green LED
}
