# Fritzing sketch crystal-ball (saved by Fritzing 0.9.3b)
breadboards: 1

parts:
  ARDUINO_UNO_R3 = Arduino Uno (Rev3)
  TILT_SWITCH = Tilt Switch [package=THT]
  R1 = Resistor [tolerance=±5% resistance=10k package=THT]
  LCD_16X2 = LCD-16X2 [package=lcd-16x2_noholes]
  R2 = Rotary Potentiometer (Small) [maximum_resistance=10kΩ package=THT]
  R3 = Resistor [tolerance=±5% resistance=220 package=THT]

nets:
  N1: ARDUINO_UNO_R3.D11_PWM/MOSI, LCD_16X2.E
  N2: ARDUINO_UNO_R3.D12/MISO, LCD_16X2.RS
  GND: ARDUINO_UNO_R3.GND, R1.Pin_1, LCD_16X2.VSS, LCD_16X2.R_W, LCD_16X2.K, R2.leg2
  N3: ARDUINO_UNO_R3.D2, LCD_16X2.DB7
  N4: ARDUINO_UNO_R3.D3_PWM, LCD_16X2.DB6
  N5: ARDUINO_UNO_R3.D4, LCD_16X2.DB5
  N6: ARDUINO_UNO_R3.D5_PWM, LCD_16X2.DB4
  N7: ARDUINO_UNO_R3.D6_PWM, TILT_SWITCH.Pin_2, R1.Pin_0
  5V: ARDUINO_UNO_R3.5V, TILT_SWITCH.Pin_1, LCD_16X2.VDD, R2.leg1, R3.Pin_0
  N8: LCD_16X2.VO, R2.wiper
  N9: LCD_16X2.A, R3.Pin_1

// code stored in the sketch: crystal-ball.ino
/**
 * Project Name: Arduino Projects Book - Project 11: Crystal Ball
 *
 * File Name: crystal-ball.ino
 *
 * Description: Use the LCD to help "predict" the future when tilting the
 * tilt switch
 *
 * Compatibility: Arduino UNO
 *
 * Phi Luu
 * Portland, Oregon, United States
 * Created August 26, 2016
 * Updated January 15, 2017
 */

#include <LiquidCrystal.h>

// Required hardware I/O connections
const byte lcdD7     = 2;  // connect D7 of the LCD to 2
const byte lcdD6     = 3;  // connect D6 of the LCD to ~3
const byte lcdD5     = 4;  // connect D5 of the LCD to 4
const byte lcdD4     = 5;  // connect D4 of the LCD to ~5
const byte lcdE      = 11; // connect E of the LCD to ~11
const byte lcdRS     = 12; // connect RS of the LCD to 12
const byte switchPin = 6;  // connect the tilt switch to ~6

// LiquidCrystal(rs, enable, d4, d5, d6, d7)
LiquidCrystal lcd(lcdRS, lcdE, lcdD4, lcdD5, lcdD6, lcdD7);

// Global constants
const byte LCDW = 16; // LCD width
const byte LCDH = 2;  // LCD height

// Global variables
byte switchVal     = 0;
byte prevSwitchVal = 0;
byte reply         = 0; // varies from 0 to 7

void setup() {
    lcd.begin(LCDW, LCDH);
    pinMode(switchPin, INPUT);
    // intro message
    lcd.setCursor(0, 0);
    lcd.print("Ask the");
    lcd.setCursor(0, 1);
    lcd.print("Crystal Ball!");
}

void loop() {
    switchVal = digitalRead(switchPin);

    if ((switchVal != prevSwitchVal) && (switchVal == LOW)) {
        reply = random(8); // randomly choose 1 out of 8 anwers
        lcd.clear();
        lcd.setCursor(0, 0);
        lcd.print("The ball says...");
        delay(1000);
        lcd.setCursor(0, 1);

        switch (reply) {
            case 0:
                lcd.print("Absolutely");
                break;
            case 1:
                lcd.print("Probably");
                break;
            case 2:
                lcd.print("Maybe");
                break;
            case 3:
                lcd.print("Yep");
                break;
            case 4:
                lcd.print("Unsure");
                break;
            case 5:
                lcd.print("Foolish Question");
                break;
            case 6:
                lcd.print("Who knows");
                break;
            case 7:
                lcd.print("Impossible");
                break;
        }
    }
    prevSwitchVal = switchVal;
}
