# Fritzing sketch dark-room (saved by Fritzing 0.9.3b)
breadboards: 1

parts:
  Arduino_UNO = Arduino Uno (Rev3)
  Photocell = PHOTOCELL [package=photocell]
  R1 = Resistor [tolerance=±10% resistance=10k package=THT]
  LED = smd LED [color="Blue (430nm)" package="0603 [SMD]"]
  R2 = Resistor [tolerance=±5% resistance=220 package=THT]

nets:
  N1: Arduino_UNO.A0, Photocell.P$2, R1.Pin_1
  N2: Arduino_UNO.D12/MISO, LED.anode
  N3: Arduino_UNO.GND, R1.Pin_0, R2.Pin_0
  N4: Arduino_UNO.5V, Photocell.P$1
  N5: LED.cathode, R2.Pin_1

// code stored in the sketch: dark-room.ino
//****************************************************************************
//
// Project Name: DIY Arduino - Project 02: Dark Room
//
// File Name: dark_room.ino
//
// Description: Automatically turn on the LED when it's dark
// Find the light switch when you come home from work at night
//
// Compatibility: Arduino UNO
//
// Phi Luu
// Portland, Oregon, United States
// Created December 13, 2015
// Updated August 13, 2016
//
//****************************************************************************

//**********Required Hardware I/O Connections**********
const int led = 12;         // connect LED to 12
const int photo = A0;       // connect photocell to A0

//**********setup**********
// Put setup code here, to run once
// Inputs: None
// Outputs: None
void setup() {
    pinMode(led, OUTPUT);   // set led as OUTPUT
}

//**********loop**********
// Put main code here, to run repeatedly
// Inputs: None
// Outputs: None
void loop() {
    int photoVal = analogRead(photo);   // read light amount from photocell
    // when you enter your room and it's too dark
    if (photoVal < 100) {
        // it will turn the light on for you
        digitalWrite(led, HIGH);
    }
    // if it's bright enough
    else {
        // turn of the LED to save energy
        digitalWrite(led, LOW);
    }
}
