# Fritzing sketch digital-hourglass (saved by Fritzing 0.9.3b)
breadboards: 1

parts:
  Arduino_UNO = Arduino Uno (Rev3)
  R1 = Resistor [tolerance=±5% resistance=10k package=THT]
  Tilt_Switch = Tilt Switch [package=THT]
  LED1 = smd LED [color="Green (555nm)" package="0603 [SMD]"]
  LED2 = smd LED [color="Red (633nm)" package="0603 [SMD]"]
  LED3 = smd LED [color="Yellow (585nm)" package="0603 [SMD]"]
  LED4 = smd LED [color="Red (633nm)" package="0603 [SMD]"]
  LED5 = smd LED [color="Green (555nm)" package="0603 [SMD]"]
  LED6 = smd LED [color="Yellow (585nm)" package="0603 [SMD]"]
  R2 = Resistor [tolerance=±5% resistance=220 package=THT]
  R3 = Resistor [tolerance=±5% resistance=220 package=THT]
  R4 = Resistor [tolerance=±5% resistance=220 package=THT]
  R5 = Resistor [tolerance=±5% resistance=220 package=THT]
  R6 = Resistor [tolerance=±5% resistance=220 package=THT]
  R7 = Resistor [tolerance=±5% resistance=220 package=THT]

nets:
  N1: Arduino_UNO.D8, R1.Pin_1, Tilt_Switch.Pin_2
  N2: Arduino_UNO.GND, R1.Pin_0, R2.Pin_0, R3.Pin_0, R4.Pin_0, R5.Pin_0, R6.Pin_0, R7.Pin_0
  N3: Arduino_UNO.D2, LED5.anode
  N4: Arduino_UNO.D3_PWM, LED6.anode
  N5: Arduino_UNO.D4, LED3.anode
  N6: Arduino_UNO.D5_PWM, LED4.anode
  N7: Arduino_UNO.D6_PWM, LED2.anode
  N8: Arduino_UNO.D7, LED1.anode
  N9: Arduino_UNO.5V, Tilt_Switch.Pin_1
  N10: LED1.cathode, R2.Pin_1
  N11: LED2.cathode, R3.Pin_1
  N12: LED3.cathode, R5.Pin_1
  N13: LED4.cathode, R4.Pin_1
  N14: LED5.cathode, R7.Pin_1
  N15: LED6.cathode, R6.Pin_1

// code stored in the sketch: digital-hourglass.ino
//****************************************************************************
//
// Project Name: Arduino Projects Book - Project 08: Digital Hourglass
//
// File Name: digital-hourglass.ino
//
// Description: A digital hourglass that turns on a LED every 2 seconds.
//   It works just like an hourglass, but digitally.
//
// Compatibility: Arduino UNO
//
// Phi Luu
// Portland, Oregon, United States
// Created July 27, 2016
// Updated August 13, 2016
//
//****************************************************************************


//**********Required Hardware I/O Connections**********
const byte switchPin = 8;   // connect tilt switch to 8
const byte led6Pin = 7;     // connect led6 to 7
const byte led5Pin = 6;     // connect led5 to ~6
const byte led4Pin = 5;     // connect led4 to ~5
const byte led3Pin = 4;     // connect led3 to 4
const byte led2Pin = 3;     // connect led2 to ~3
const byte led1Pin = 2;     // connect led1 to 2

unsigned long prevTime = 0; // hold the time
byte currSwitchState = 0;   // hold the current switch state
byte prevSwitchState = 0;   // hold the previous switch state
byte currLed = led1Pin;     // init the current led to be led1
unsigned long interval = 2000;      // 2 seconds = 2,000 milliseconds
                                    // between each event

//**********setup**********
// Put setup code here, to run once
// Inputs: None
// Outputs: None
void setup() {
    // set all LED pins as OUTPUT
    for (byte led = led1Pin; led <= led6Pin; led++) {
        pinMode(led, OUTPUT);
    }
    // set switch pin as INPUT
    pinMode(switchPin, INPUT);
}

//**********loop**********
// Put main code here, to run repeatedly
// Inputs: None
// Outputs: None
void loop() {
    // start the timer and set the new current time
    unsigned long currTime = millis();
    // check the time
    if (currTime - prevTime > interval) {
        prevTime = currTime;            // store the current time
        digitalWrite(currLed, HIGH);    // turn on the current LED
        // once the time is up (all LEDs are turned on)
        if (currLed == led6Pin) {
            // make a flashing effect
            // indicating that time is up
            for (byte t = 0; t < 4; t++) {
                for (byte led = led1Pin; led <= led6Pin; led++) {
                    digitalWrite(led, HIGH);    // flashing on
                }
                if (t < 3) {
                    delay(250);     // for 0.25 second
                }
                else {
                    delay(1000);    // the last flash takes 1 second
                }
                for (byte led = led1Pin; led <= led6Pin; led++) {
                    digitalWrite(led, LOW);     // flashing off
                }
                delay(250);                     // for 0.25 second
            }
            // restart the process
            currLed = led1Pin;
        }
        else {
            currLed++;  // next LED
        }
    }

    // read the current switch state from the tilt switch
    currSwitchState = digitalRead(switchPin);
    // check difference in the switch states
    // simulate the flip of the hourglass. If the hourglass is flipped
    if (currSwitchState != prevSwitchState) {
        // restart the process
        // turn off all LEDs
        for (byte led = led1Pin; led <= led6Pin; led++) {
            digitalWrite(led, LOW);
        }
        // go back to the first LED
        currLed = led1Pin;
        // store the current time
        prevTime = currTime;
    }
    // store the current switch state
    prevSwitchState = currSwitchState;
}
