# Fritzing sketch keyboard-instrument (saved by Fritzing 0.9.3b)
breadboards: 1

parts:
  Arduino_UNO = Arduino Uno (Rev3)
  Piezo_Buzzer = Piezo Speaker
  S1 = Pushbutton [package="[SMD]"]
  S2 = Pushbutton [package="[SMD]"]
  S3 = Pushbutton [package="[SMD]"]
  R1 = Resistor [tolerance=±5% resistance=220 package=THT]
  R2 = Resistor [tolerance=±5% resistance=10k package=THT]
  R3 = Resistor [tolerance=±5% resistance=1M package=THT]
  R4 = Resistor [tolerance=±5% resistance=10k package=THT]
  S4 = Pushbutton [package="[SMD]"]

nets:
  N1: Arduino_UNO.A0, S1.Pin_3, S1.Pin_4, S2.Pin_3, S2.Pin_4, S3.Pin_3, S3.Pin_4, R4.Pin_1, S4.Pin_3, S4.Pin_4
  N2: Arduino_UNO.D8, Piezo_Buzzer.pin2
  N3: Arduino_UNO.GND, Piezo_Buzzer.pin1, R4.Pin_0
  N4: Arduino_UNO.5V, S1.Pin_1, S1.Pin_2, R1.Pin_0, R2.Pin_0, R3.Pin_0
  N5: S2.Pin_1, S2.Pin_2, R1.Pin_1
  N6: S3.Pin_1, S3.Pin_2, R2.Pin_1
  N7: R3.Pin_1, S4.Pin_1, S4.Pin_2

// code stored in the sketch: keyboard-instrument.ino
//****************************************************************************
//
// Project Name: Arduino Projects Book - Project 07: Keyboard Instrument
//
// File Name: keyboard_instrument.ino
//
// Description: Simulate keys C, D, E, and F of the real piano
// using push buttons and piezo buzzer
//
// Compatibility: Arduino UNO
//
// Phi Luu
// Portland, Oregon, United States
// Created March 05, 2016
// Updated August 13, 2016
//
//****************************************************************************

//**********Required Hardware I/O Connections**********
const int piezo = 8;        // connect buzzer to 8
const int keyboard = A0;    // connect keyboard to A0

// define frequencies for C, D, E, and F in the real piano
const int notes[] = {262, 294, 330, 349};

// baud rate for serial monitor
const unsigned int BAUD_RATE = 9600;

//**********setup**********
// Put setup code here, to run once
// Inputs: None
// Outputs: None
void setup() {
    Serial.begin(BAUD_RATE);    // start the serial monitor
    pinMode(piezo, OUTPUT);     // set piezo as OUTPUT
}

//**********loop**********
// Put main code here, to run repeatedly
// Inputs: None
// Outputs: None
void loop() {
    // read input from the keyboard and set to keyVal
    unsigned int keyVal = analogRead(keyboard);
    Serial.print("keyVal = ");
    Serial.println(keyVal); // indicate the value of keyVal for debugging
    // if the first button is pressed
    if (keyVal == 1023) {
        tone(piezo, notes[0]);      // play key C of the real piano
    }
    // if the second button is pressed
    else if (keyVal >= 990 && keyVal <= 1010) {
        tone(piezo, notes[1]);      // play key D of the real piano
    }
    // if the third button is pressed
    else if (keyVal >= 505 && keyVal <= 515) {
        tone(piezo, notes[2]);      // play key E of the real piano
    }
    // if the fourth button is pressed
    else if (keyVal >= 5 && keyVal <= 10) {
        tone(piezo, notes[3]);      // play key F of the real piano
    }
    // if no button is pressed (or out of tolerance)
    else {
        noTone(piezo);              // mute the piezo
    }
}
a
