# Fritzing sketch keyboard_instrument (saved by Fritzing 0.9.3b)
breadboards: 1

parts:
  ARDUINO_UNO_R3 = Arduino Uno (Rev3)
  PIEZO_BUZZER = Piezo Speaker
  S1 = Pushbutton [package="[SMD]"]
  S2 = Pushbutton [package="[SMD]"]
  S3 = Pushbutton [package="[SMD]"]
  R1 = Resistor [tolerance=±5% resistance=220 package=THT]
  R2 = Resistor [tolerance=±5% resistance=10k package=THT]
  R3 = Resistor [tolerance=±5% resistance=1M package=THT]
  R4 = Resistor [tolerance=±5% resistance=10k package=THT]
  S4 = Pushbutton [package="[SMD]"]

nets:
  N1: ARDUINO_UNO_R3.A0, S1.Pin_3, S1.Pin_4, S2.Pin_3, S2.Pin_4, S3.Pin_3, S3.Pin_4, R4.Pin_1, S4.Pin_3, S4.Pin_4
  N2: ARDUINO_UNO_R3.D8, PIEZO_BUZZER.pin2
  N3: ARDUINO_UNO_R3.GND, PIEZO_BUZZER.pin1, R4.Pin_0
  N4: ARDUINO_UNO_R3.5V, S1.Pin_1, S1.Pin_2, R1.Pin_0, R2.Pin_0, R3.Pin_0
  N5: S2.Pin_1, S2.Pin_2, R1.Pin_1
  N6: S3.Pin_1, S3.Pin_2, R2.Pin_1
  N7: R3.Pin_1, S4.Pin_1, S4.Pin_2

// code stored in the sketch: keyboard-instrument.ino
/**
 * Project Name: Arduino Projects Book - Project 07: Keyboard Instrument
 *
 * File Name: keyboard_instrument.ino
 *
 * Description: Simulate keys C, D, E, and F of the real piano
 * using push buttons and piezo buzzer
 *
 * Compatibility: Arduino UNO
 *
 * Phi Luu
 * Portland, Oregon, United States
 * Created March 05, 2016
 * Updated January 15, 2017
 */

// Required hardware I/O connections
const byte keyboard = A0;                   // connect keyboard to A0
const byte piezoPin = 8;                    // connect buzzer to 8

// Global constants
const int notes[] = { 262, 294, 330, 349 }; // C, D, E, F frequencies
const unsigned int BAUD_RATE = 9600;        // serial monitor's baud rate

// Global variables
unsigned int keyVal;

void setup() {
    Serial.begin(BAUD_RATE);   // start the serial monitor
    pinMode(piezoPin, OUTPUT); // set piezoPin as OUTPUT
}

void loop() {
    // read and print keyboard value
    keyVal = analogRead(keyboard);
    Serial.print("keyVal = ");
    Serial.println(keyVal);

    if (keyVal == 1023) {
        tone(piezoPin, notes[0]); // first switch ~ key C
    } else if ((keyVal >= 990) && (keyVal <= 1010)) {
        tone(piezoPin, notes[1]); // second switch ~ key D
    } else if ((keyVal >= 505) && (keyVal <= 515)) {
        tone(piezoPin, notes[2]); // third switch ~ key E
    } else if ((keyVal >= 5) && (keyVal <= 10)) {
        tone(piezoPin, notes[3]); // fourth switch ~ key F
    } else {
        noTone(piezoPin);         // no switch ~ no sound
    }
}
