# Fritzing sketch knock-lock (saved by Fritzing 0.9.3b)
breadboards: 1

parts:
  ARDUINO_UNO_R3 = Arduino Uno (Rev3)
  PIEZO_BUZZER = Piezo Speaker
  R1 = Resistor [tolerance=±5% resistance=1M package=THT]
  S1 = Pushbutton [package="[SMD]"]
  R2 = Resistor [tolerance=±5% resistance=10k package=THT]
  LED1 = smd LED [color="Red (633nm)" package="0603 [SMD]"]
  LED2 = smd LED [color="Green (555nm)" package="0603 [SMD]"]
  LED3 = smd LED [color="Yellow (585nm)" package="0603 [SMD]"]
  R3 = Resistor [tolerance=±5% resistance=220 package=THT]
  R4 = Resistor [tolerance=±5% resistance=220 package=THT]
  R5 = Resistor [tolerance=±5% resistance=220 package=THT]
  SERVO_MOTOR = Dagu DGServo 9g (Pan and tilt) [part_number=RS001B]
  C1 = Electrolytic Capacitor [capacitance=100µF package="200 mil [THT, electrolytic]"]

nets:
  N1: ARDUINO_UNO_R3.A0, PIEZO_BUZZER.pin1, R1.Pin_0
  N2: ARDUINO_UNO_R3.D9_PWM, SERVO_MOTOR.pulse
  N3: ARDUINO_UNO_R3.D2, S1.Pin_1, S1.Pin_2, R2.Pin_0
  N4: ARDUINO_UNO_R3.D3_PWM, LED3.anode
  N5: ARDUINO_UNO_R3.D4, LED2.anode
  N6: ARDUINO_UNO_R3.D5_PWM, LED1.anode
  5V: ARDUINO_UNO_R3.5V, PIEZO_BUZZER.pin2, S1.Pin_3, S1.Pin_4, SERVO_MOTOR.vcc, C1.+
  GND: ARDUINO_UNO_R3.GND, R1.Pin_1, R2.Pin_1, R3.Pin_1, R4.Pin_1, R5.Pin_1, SERVO_MOTOR.gnd, C1.-
  N7: LED1.cathode, R3.Pin_0
  N8: LED2.cathode, R4.Pin_0
  N9: LED3.cathode, R5.Pin_0

// code stored in the sketch: knock-lock.ino
/**
 * Project Name: Arduino Projects Book - Project 12: Knock Lock
 *
 * File Name: knock-lock.ino
 *
 * Description: Using the Piezo buzzer to make a secret locking mechanism, in
 * order to keep intruders out
 *
 * Compatibility: Arduino UNO
 *
 * Phi Luu
 * Portland, Oregon, United States
 * Created September 06, 2016
 * Updated January 15, 2017
 */

#include <Servo.h>
Servo servoMotor;

// Required hardware I/O connections
const byte piezoPin     = A0; // the pin piezo buzzer connected to
const byte switchPin    = 2;  // the pin switch connected to
const byte yellowLEDPin = 3;  // the pin yellow LED connected to
const byte greenLEDPin  = 4;  // the pin green LED connnected to
const byte redLEDPin    = 5;  // the pin red LED connected to
const byte servoPin     = 9;  // the pin servo motor connected to

// Global constants
const unsigned short baudRate = 9600;
const byte quietKnockVal      = 30;
const byte loudKnockVal       = 50;
const byte maxNumKnock        = 5;

// Global variables
byte switchVal;
byte knockVal;
boolean locked    = false;
byte    numKnocks = 0;

void setup() {
    servoMotor.attach(servoPin);
    pinMode(switchPin,    INPUT);
    pinMode(yellowLEDPin, OUTPUT);
    pinMode(greenLEDPin,  OUTPUT);
    pinMode(redLEDPin,    OUTPUT);
    Serial.begin(baudRate);
    // unlock the box first
    digitalWrite(greenLEDPin, HIGH);
    servoMotor.write(0);
    Serial.println("ACCESS GRANTED");
}

void loop() {
    if (locked == false) {
        switchVal = digitalRead(switchPin);

        if (switchVal == HIGH) {
            lockTheBox();
        }
    } else {
        knockVal = analogRead(piezoPin);

        // require maxNumKnock valid knocks
        if ((numKnocks < maxNumKnock) && (knockVal > 0)) {
            if (checkForKnock(knockVal) == true) {
                numKnocks++;
            }
            Serial.print("Need ");
            Serial.print(maxNumKnock - numKnocks);
            Serial.println(" more knock(s)");
        }

        if (numKnocks >= maxNumKnock) {
            unlockTheBox();
            // reset numKnocks
            numKnocks = 0;
        }
    }
}

/**
 * Changes the LEDs and turn the servo to unlock the box
 */
void unlockTheBox(void) {
    // change the locked value
    locked = false;
    // indicate on LEDs
    digitalWrite(redLEDPin,   LOW);
    digitalWrite(greenLEDPin, HIGH);
    // rotate the servo to 0 degree
    servoMotor.write(0);
    // print a message on the Serial Monitor
    Serial.println("ACCESS GRANTED");
    // allow time for the servo to completely move
    delay(20);
}

/**
 * Changes the LEDs and turn the servo to lock the box
 */
void lockTheBox(void) {
    // change locked value
    locked = true;
    // indicate on LEDs
    digitalWrite(greenLEDPin, LOW);
    digitalWrite(redLEDPin,   HIGH);
    // rotate the servo to 90 degrees
    servoMotor.write(90); // rotate the servo 90 degrees to lock
    // print a message on the Serial Monitor
    Serial.println("ACCESS DENIED");
    // allow time for the servo to completely move
    delay(20);
}

/**
 * Checks to see if a knock is valid or not
 *
 * @param   aKnockVal   the loudness of the knock
 *
 * @return  true        a valid knock
 * @return  false       an invalid knock
 */
boolean checkForKnock(byte aKnockVal) {
    if ((aKnockVal > quietKnockVal) && (aKnockVal < loudKnockVal)) {
        digitalWrite(yellowLEDPin, HIGH);
        delay(50);
        digitalWrite(yellowLEDPin, LOW);
        Serial.print("Valid knock value: ");
        Serial.println(aKnockVal);
        return true;
    } else {
        Serial.print("Invalid knock value: ");
        Serial.println(aKnockVal);
        return false;
    }
}
