# Fritzing sketch letter-p (saved by Fritzing 0.9.3b)
breadboards: 1

parts:
  Arduino_UNO = Arduino Uno (Rev3)
  R1 = Resistor [tolerance=±5% resistance=220 package=THT]
  R2 = Resistor [tolerance=±5% resistance=220 package=THT]
  R3 = Resistor [tolerance=±5% resistance=220 package=THT]
  R4 = Resistor [tolerance=±5% resistance=220 package=THT]
  R5 = Resistor [tolerance=±5% resistance=220 package=THT]
  R6 = Resistor [tolerance=±5% resistance=220 package=THT]
  LED4 = smd LED [color="Red (633nm)" package="0603 [SMD]"]
  LED3 = smd LED [color="Red (633nm)" package="0603 [SMD]"]
  LED2 = smd LED [color="Red (633nm)" package="0603 [SMD]"]
  LED1 = smd LED [color="Red (633nm)" package="0603 [SMD]"]
  LED6 = smd LED [color="Red (633nm)" package="0603 [SMD]"]
  LED5 = smd LED [color="Red (633nm)" package="0603 [SMD]"]

nets:
  N1: Arduino_UNO.D2, LED1.anode
  N2: Arduino_UNO.D3_PWM, LED2.anode
  N3: Arduino_UNO.D4, LED3.anode
  N4: Arduino_UNO.D5_PWM, LED4.anode
  N5: Arduino_UNO.D6_PWM, LED6.anode
  N6: Arduino_UNO.D7, LED5.anode
  N7: Arduino_UNO.GND, R1.Pin_0, R2.Pin_0, R3.Pin_0, R4.Pin_0, R5.Pin_1, R6.Pin_1
  N8: R1.Pin_1, LED1.cathode
  N9: R2.Pin_1, LED2.cathode
  N10: R3.Pin_1, LED3.cathode
  N11: R4.Pin_1, LED4.cathode
  N12: R5.Pin_0, LED6.cathode
  N13: R6.Pin_0, LED5.cathode

// code stored in the sketch: letter-p.ino
// ****************************************************************************
//
// Project Name: DIY Arduino - Project 01: Letter P
//
// File Name: letter_p.ino
//
// Description: Make a beautiful effect of letter P
//
// Compatibility: Arduino UNO
//
// Phi Luu
// Portland, Oregon, United States
// Created September 29, 2015
// Updated August 13, 2016
//
// ****************************************************************************

// LEDs arrangement
// LED4 LED5
// LED3 LED6
// LED2
// LED1

//**********Required Hardware I/O Connections**********
const byte LED1 = 2;     // connect LED 1 to 2
const byte LED2 = 3;     // connect LED 2 to ~3
const byte LED3 = 4;     // connect LED3 to 4
const byte LED4 = 5;     // connect LED4 to ~5
const byte LED5 = 6;     // connect LED5 to ~6
const byte LED6 = 7;     // connect LED6 to 7

// set how long in milliseconds to flash one LED
const unsigned int TIME = 100;

//**********setup**********
// Put setup code here, to run once
// Inputs: None
// Outputs: None
void setup() {
    for (byte pinNumber = LED1; pinNumber <= LED6; pinNumber++) {
        pinMode(pinNumber, OUTPUT);    // set pin 2 to pin 8 as OUTPUT
    }
}

//**********loop**********
// Put main code here, to run repeatedly
// Inputs: None
// Outputs: None
void loop() {
    for (byte pinNumber = LED1; pinNumber <= LED6; pinNumber++) {
        digitalWrite(pinNumber, LOW);   // turn off all LED
    }
    digitalWrite(LED1, HIGH);  // start with LED 1
    delay(TIME);               // flash this LED for TIME milliseconds
    // create a "running" effect on LEDs
    for (byte pinNumber = LED1; pinNumber <= LED5; pinNumber++) {
        digitalWrite(pinNumber, LOW);       // turn off this LED
        digitalWrite(pinNumber + 1, HIGH);  // and turn on next LED
        delay(TIME);                        // turn on for TIME milliseconds
    }
    // when completes letter P, go straight down and repeat it again
    digitalWrite(LED6, LOW);
    digitalWrite(LED3, HIGH);
    delay(TIME);
    digitalWrite(LED3, LOW);
    digitalWrite(LED2, HIGH);
    delay(TIME);
    digitalWrite(LED2, LOW);
    digitalWrite(LED1, HIGH);
}
