# Fritzing sketch light-theremin (saved by Fritzing 0.9.3b)
breadboards: 1

parts:
  Arduino_UNO = Arduino Uno (Rev3)
  Photocell = PHOTOCELL [package=photocell]
  R1 = Resistor [tolerance=±5% resistance=10k package=THT]
  Piezo_Buzzer = Piezo Speaker
  LED = smd LED [color="Red (633nm)" package="0603 [SMD]"]
  R2 = Resistor [tolerance=±5% resistance=220 package=THT]

nets:
  N1: Arduino_UNO.A0, Photocell.P$2, R1.Pin_1
  N2: Arduino_UNO.D2, Piezo_Buzzer.pin2
  N3: Arduino_UNO.D4, LED.anode
  N4: Arduino_UNO.5V, Photocell.P$1
  N5: Arduino_UNO.GND, R1.Pin_0, Piezo_Buzzer.pin1, R2.Pin_0
  N6: LED.cathode, R2.Pin_1

// code stored in the sketch: light-theremin.ino
//****************************************************************************
//
// Project Name: Arduino Projects Book - Project 06: Light Theremin
//
// File Name: light_theremin.ino
//
// Description: Make a light-based theremin using photocells and a buzzer
//
// Compatibility: Arduino UNO
//
// Phi Luu
// Portland, Oregon, United States
// Created January 10, 2016
// Updated August 13, 2016
//
//****************************************************************************

//**********Required Hardware I/O Connections**********
const byte sensorPin = A0;     // connect photocell to A0
const byte ledPin = 4;         // connect LED to 4
const byte piezoPin = 2;       // connect buzzer to 2

unsigned int sensorValue;        // declare sensorValue
unsigned int sensorHigh = 0;     // 0 as the initial min of the photocell
unsigned int sensorLow = 1023;   // 1023 as the initial max of the photocell

//**********setup**********
// Put setup code here, to run once
// Inputs: None
// Outputs: None
void setup() {
    pinMode(ledPin, OUTPUT);
    digitalWrite(ledPin, HIGH); // red light is turning on - calibrating...
    // calibrate the photocell for 5 seconds
    while (millis() < 5000) {
        sensorValue = analogRead(sensorPin);    // read sensorPin value
        if (sensorValue > sensorHigh) {
            sensorHigh = sensorValue;   // set upper bound of the photocell
        }
        if (sensorValue < sensorLow) {
            sensorLow = sensorValue;    // set lower bound of the photocell
        }
    }
    // calibration completed
    digitalWrite(ledPin, LOW);  // red light turned off
}

//**********loop**********
// Put main code here, to run repeatedly
// Inputs: None
// Outputs: None
void loop() {
    sensorValue = analogRead(sensorPin);    // read sensorPin value again
    // determine the pitch of the piezo
    unsigned int pitch = map(sensorValue, sensorLow, sensorHigh, 50, 4000);
    // play the piezo with the pitch above and play for 20 milliseconds
    tone(piezoPin, pitch, 20);
    delay(10);                              // wait 10 milliseconds
}
