# Fritzing sketch mood_cue (saved by Fritzing 0.9.3b)
breadboards: 1

parts:
  ARDUINO_UNO_R3 = Arduino Uno (Rev3)
  C1 = Electrolytic Capacitor [capacitance=100µF voltage=25V package="200 mil [THT, electrolytic]"]
  C2 = Electrolytic Capacitor [capacitance=100µF voltage=25V package="200 mil [THT, electrolytic]"]
  M1 = Dagu DGServo 9g (Top view) [part_number=RS001B]
  R1 = Rotary Potentiometer (Small) [maximum_resistance=10kΩ package=THT]

nets:
  N1: ARDUINO_UNO_R3.A0, R1.wiper
  GND: ARDUINO_UNO_R3.GND, C1.-, C2.-, M1.gnd, R1.leg1
  N2: ARDUINO_UNO_R3.D3_PWM, M1.pulse
  5V: ARDUINO_UNO_R3.5V, C1.+, C2.+, M1.vcc, R1.leg2

// code stored in the sketch: mood-cue.ino
/**
 * Project Name: Arduino Projects Book - Project 05: Mood Cue
 *
 * File Name: mood_cue.ino
 *
 * Description: Express your feeling by a servo motor
 *
 * Compatibility: Arduino UNO
 *
 * Phi Luu
 * Portland, Oregon, United States
 * Created November 21, 2015
 * Updated January 15, 2017
 */

// include Servo library for servo motors
#include <Servo.h>

// Required hardware I/O connections
const byte potPin   = A0;            // connect potentiometer to A0
const byte servoPin = 3;             // connect servo motor to ~3

// Servo class
Servo myServo;                       // declare myServo

// Global constants
const unsigned int BAUD_RATE = 9600; // serial monitor's baud rate

// Global variables
unsigned int  potVal;                // potentiometer
unsigned char angle;                 // servo's angle

void setup() {
    myServo.attach(servoPin);        // attach myServo into servoPin
    Serial.begin(BAUD_RATE);         // start the Serial Monitor
}

void loop() {
    // read & print potentiometer value
    potVal = analogRead(potPin);
    Serial.print("potVal: ");
    Serial.print(potVal);
    // map & print from pot value to angle
    angle = map(potVal, 0, 1023, 0, 179);
    Serial.print(", angle: ");
    Serial.println(angle);
    // run the servo by the angle
    myServo.write(angle);
    // delay to stabilize
    delay(15);
}
