# Fritzing sketch motorized-pinwheel (saved by Fritzing 0.9.3b)
breadboards: 1

parts:
  Arduino_UNO = Arduino Uno (Rev3)
  Switch = Pushbutton [package="[SMD]"]
  R = Resistor [tolerance=±5% resistance=10k package=THT]
  MOSFET = Basic FET N-Channel [package="TO220 [THT]"]
  VCC1 = Battery block 9V
  Diode = Rectifier Diode [part_number=1N4001 package="Melf DO-213 AB [SMD]"]
  DC_Motor = DC Motor

nets:
  N1: Arduino_UNO.D9_PWM, MOSFET.gate
  N2: Arduino_UNO.D2, Switch.Pin_3, Switch.Pin_4, R.Pin_1
  N3: Arduino_UNO.5V, Switch.Pin_1, Switch.Pin_2
  N4: Arduino_UNO.GND, R.Pin_0, MOSFET.source, VCC1.-
  N5: MOSFET.drain, Diode.anode, DC_Motor.pin_1
  N6: VCC1.+, Diode.cathode, DC_Motor.pin_2

// code stored in the sketch: motorized-pinwheel.ino
//****************************************************************************
//
// Project Name: Arduino Projects Book - Project 09: Motorized Pinwheel
//
// File Name: motorized-pinwheel.ino
//
// Description: Get the Arduino to spin a colorful pinwheel using a motor
//
// Compatibility: Arduino UNO
//
// Phi Luu
// Portland, Oregon, United States
// Created August 13, 2016
// Updated August 13, 2016
//
//****************************************************************************

//**********Required Hardware I/O Connections**********
const byte switchPin = 2;       // connect switch to 2
const byte motorPin = 9;        // connect dc motor to ~9

//**********setup**********
// Put setup code here, to run once
// Inputs: None
// Outputs: None
void setup() {
    pinMode(switchPin, INPUT);
    pinMode(motorPin, OUTPUT);
}

//**********loop**********
// Put main code here, to run repeatedly
// Inputs: None
// Outputs: None
void loop() {
    byte switchState = digitalRead(switchPin);   // read input from the switch
    // if the switch is pressed
    if (switchState) {
        digitalWrite(motorPin, HIGH);       // spin the motor
    }
    // otherwise
    else {
        digitalWrite(motorPin, LOW);        // cut the power from the motor
    }
}
