# Fritzing sketch motorized_pinwheel (saved by Fritzing 0.9.3b)
breadboards: 1

parts:
  ARDUINO_UNO_R3 = Arduino Uno (Rev3)
  ON/OFF = Pushbutton [package="[SMD]"]
  R = Resistor [tolerance=±5% resistance=10k package=THT]
  MOSFET = Basic FET N-Channel [package="TO220 [THT]"]
  VCC1 = Battery block 9V
  DIODE = Rectifier Diode [part_number=1N4001 package="Melf DO-213 AB [SMD]"]
  DC_MOTOR = DC Motor

nets:
  N1: ARDUINO_UNO_R3.D9_PWM, MOSFET.gate
  N2: ARDUINO_UNO_R3.D2, ON/OFF.Pin_3, ON/OFF.Pin_4, R.Pin_1
  N3: ARDUINO_UNO_R3.5V, ON/OFF.Pin_1, ON/OFF.Pin_2
  N4: ARDUINO_UNO_R3.GND, R.Pin_0, MOSFET.source, VCC1.-
  N5: MOSFET.drain, DIODE.anode, DC_MOTOR.pin_1
  N6: VCC1.+, DIODE.cathode, DC_MOTOR.pin_2

// code stored in the sketch: motorized-pinwheel.ino
/**
 * Project Name: Arduino Projects Book - Project 09: Motorized Pinwheel
 *
 * File Name: motorized-pinwheel.ino
 *
 * Description: Get the Arduino to spin a colorful pinwheel using a motor
 *
 * Compatibility: Arduino UNO
 *
 * Phi Luu
 * Portland, Oregon, United States
 * Created August 13, 2016
 * Updated January 15, 2017
 */

// Required hardware I/O connections
const byte switchPin = 2; // connect switch to 2
const byte motorPin  = 9; // connect dc motor to ~9

void setup() {
    pinMode(switchPin, INPUT);
    pinMode(motorPin,  OUTPUT);
}

void loop() {
    byte switchState = digitalRead(switchPin);

    // toggle the switch to toggle the motor
    if (switchState) {
        digitalWrite(motorPin, HIGH);
    } else {
        digitalWrite(motorPin, LOW);
    }
}
