# Fritzing sketch touchy-feely-lamp (saved by Fritzing 0.9.3b)
breadboards: 1

parts:
  Arduino_UNO = Arduino Uno (Rev3)
  LED = smd LED [color="Blue (470nm)" package="0603 [SMD]"]
  R1 = Resistor [tolerance=±5% resistance=220 package=THT]
  R2 = Resistor [tolerance=±5% resistance=1M package=THT]
  A_piece_of_conductive_material = Ceramic Capacitor [capacitance=100nF package="100 mil [THT, multilayer]"]

nets:
  N1: Arduino_UNO.D12/MISO, LED.anode
  N2: Arduino_UNO.GND, R1.Pin_0
  N3: Arduino_UNO.D2, R2.Pin_1, A_piece_of_conductive_material.0
  N4: Arduino_UNO.D4, R2.Pin_0
  N5: LED.cathode, R1.Pin_1

// code stored in the sketch: touchy-feely-lamp.ino
//****************************************************************************
//
// Project Name: Arduino Projects Book - Project 13: Touchy-feely Lamp
//
// File Name: touchy-feely-lamp.ino
//
// Description: Use the capacitance of  your body to turn an LED on/off
// when you touch a piece of conductive material.
//
// Compatibility: Arduino UNO
//
// Phi Luu
// Portland, Oregon, United States
// Created December 18, 2016
// Updated December 18, 2016
//
//****************************************************************************

//**********Required Hardware Connections**********
const byte sendingPin = 4;        // capacitance sending pin connected to 4
const byte receivingPin = 2;      // capacitance receiving pin connected to 2
const byte ledPin = 12;           // indicator LED pin connected to 12

#include <CapacitiveSensor.h>
CapacitiveSensor capSensor = CapacitiveSensor(sendingPin, receivingPin);

// different people may set different capacitance threshold. I set it to 50
const int threshold = 45;
const unsigned short BAUD_RATE = 9600;

// Put setup code here, to run once
void setup() {
    Serial.begin(BAUD_RATE);
    pinMode(ledPin, OUTPUT);
}

// Put main code here, to run repeatedly
void loop() {
    // read 30 samples at a time
    int sensorValue = capSensor.capacitiveSensor(30);
    Serial.print("Sensor value: ");
    Serial.println(sensorValue);

    // turn on the LED if the capacitance is over the threshold
    if (sensorValue > threshold) {
        digitalWrite(ledPin, HIGH);
    }
    else {
        digitalWrite(ledPin, LOW);
    }

    // delay helps stablizing the sensor
    delay(10);
}
