# Fritzing sketch tweak-the-arduino-logo (saved by Fritzing 0.9.3b)
breadboards: 1

parts:
  Arduino_UNO = Arduino Uno (Rev3)
  Potentiometer = Rotary Potentiometer (Small) [maximum_resistance=100kΩ package=THT]

nets:
  N1: Arduino_UNO.A0, Potentiometer.wiper
  N2: Arduino_UNO.GND, Potentiometer.leg2
  N3: Arduino_UNO.5V, Potentiometer.leg1

// code stored in the sketch: tweak-the-arduino-logo.ino
//****************************************************************************
//
// Project Name: Arduino Projects Book - Project 14: Tweak the Arduino Logo
//
// File Name: teak-the-arduino-logo.ino
//
// Description: Using serial communication, the Arduino can send and receive
// information to the computer. Draw the Arduino logo on the computer screen
// by the potentiometer on the Arduino
//
// Compatibility: Arduino UNO
//
// Phi Luu
// Portland, Oregon, United States
// Created January 07, 2017
// Updated January 07, 2017
//
//****************************************************************************

//***
// Global declaration
//***

// Required hardware I/O connections
const byte potPin = A0;                // potentiometer connected to A0

// Global constants
const unsigned short BAUD_RATE = 9600; // for serial monitor

//***
// Mandatory Routines
//***

void setup() {
    Serial.begin(BAUD_RATE);
}

void loop() {
    // potentiometer reads values from 0 to 1024
    // map it to 0-255 to speed up the communication
    Serial.write(analogRead(potPin) / 4);
    delay(1); // stabilize the pot
}
