# Fritzing sketch zoetrope (saved by Fritzing 0.9.3b)
breadboards: 1

parts:
  Arduino_UNO = Arduino Uno (Rev3)
  S1 = Pushbutton [package="[SMD]"]
  S2 = Pushbutton [package="[SMD]"]
  R1 = Resistor [tolerance=±5% resistance=10k package=THT]
  R2 = Resistor [tolerance=±5% resistance=10k package=THT]
  Battery = Battery block 9V
  R3 = Rotary Potentiometer (Small) [maximum_resistance=100kΩ package=THT]
  H-Bridge_IC = L293D [package=THT]
  DC_Motor = DC Motor

nets:
  N1: Arduino_UNO.A0, R3.wiper
  N2: Arduino_UNO.D9_PWM, H-Bridge_IC.Enable_1
  N3: Arduino_UNO.GND, R1.Pin_1, R2.Pin_1, Battery.-, R3.leg2, H-Bridge_IC.0V
  N4: Arduino_UNO.D2, H-Bridge_IC.In_2
  N5: Arduino_UNO.D3_PWM, H-Bridge_IC.In_1
  N6: Arduino_UNO.D4, S2.Pin_3, S2.Pin_4, R2.Pin_0
  N7: Arduino_UNO.D5_PWM, S1.Pin_3, S1.Pin_4, R1.Pin_0
  N8: Arduino_UNO.5V, S1.Pin_1, S1.Pin_2, S2.Pin_1, S2.Pin_2, R3.leg1, H-Bridge_IC.+V
  N9: Battery.+, H-Bridge_IC.+Vmotor
  N10: H-Bridge_IC.Out_1_(_Controlled_by_Enable_1_), DC_Motor.pin_1
  N11: H-Bridge_IC.Out_2_(_Controlled_by_Enable_1_), DC_Motor.pin_2

// code stored in the sketch: zoetrope.ino
//****************************************************************************
//
// Project Name: Arduino Projects Book - Project 10: Zoetrope
//
// File Name: zoetrope.ino
//
// Description: Control the speed and the direction of the DC motor using
// two switches and a potentiometer
//
// Compatibility: Arduino UNO
//
// Phi Luu
// Portland, Oregon, United States
// Created August 21, 2016
// Updated August 21, 2016
//
//****************************************************************************

//**********Required Hardware I/O Connections**********
const byte icInput1 = 3;        // connect IC Input1 to ~3
const byte icInput2 = 2;        // connect IC Input2 to 2
const byte icEnable1 = 9;       // connect IC Enable1 t ~9
const byte dirSwitch = 4;       // connect direction switch to 4
const byte stateSwitch = 5;     // connect state switch to ~5
const byte potPin = A0;         // connect potentiometer to A0

byte stateSwitchVal = 0;        // hold values of state switch
byte dirSwitchVal = 0;          // hold values of direction switch
byte prevStateSwitchVal = 0;    // hold the previous value of state switch
byte prevDirSwitchVal = 0;      // hold the previous value of direction switch

byte motorEnabled = 0;          // indicate whether the motor is on/off
byte motorDirection = 0;        // indicate the motor direction
unsigned short motorSpeed = 0;  // control the motor speed


//**********setup**********
// Put setup code here, to run once
// Inputs: None
// Outputs: None
void setup() {
    pinMode(dirSwitch, INPUT);
    pinMode(stateSwitch, INPUT);
    pinMode(icInput1, OUTPUT);
    pinMode(icInput2, OUTPUT);
    pinMode(icEnable1, OUTPUT);
}

//**********loop**********
// Put main code here, to run repeatedly
// Inputs: None
// Outputs: None
void loop() {
    stateSwitchVal = digitalRead(stateSwitch);
    delay(1);       // delay helps the Arduino stable
    dirSwitchVal = digitalRead(dirSwitch);
    motorSpeed = analogRead(potPin)/4;

    // process the on/off state of the motor from the state switch
    if (stateSwitchVal != prevStateSwitchVal) {
        if (stateSwitchVal) {
            motorEnabled = !motorEnabled;
        }
    }

    // process the direction of the motor from the direction switch
    if (dirSwitchVal != prevDirSwitchVal) {
        if (dirSwitchVal) {
            motorDirection = !motorDirection;
        }
    }

    // control the direction of the motor using the IC
    if (motorDirection) {
        digitalWrite(icInput1, LOW);
        digitalWrite(icInput2, HIGH);
    }
    else {
        digitalWrite(icInput1, HIGH);
        digitalWrite(icInput2, LOW);
    }

    // control the on/off state of the motor using PWM
    if (motorEnabled) {
        analogWrite(icEnable1, motorSpeed);
    }
    else {
        analogWrite(icEnable1, 0);
    }

    // prep for next inputs
    prevStateSwitchVal = stateSwitchVal;
    prevDirSwitchVal = dirSwitchVal;
}
